# Fritzing sketch conexiones (saved by Fritzing 0.9.3b)
breadboards: 1

parts:
  U1 = NodeMCU V1.0
  DHT1 = DHT11 Humitidy and Temperature Sensor
  Part1 = FC-28 Soil Hygrometer Module - Probe
  Part2 = FC-28 Soil Hygrometer Module
  J1 = Basic Servo

nets:
  N1: U1.D1, J1.pulse
  N2: U1.D2, DHT1.DATA
  VCC: U1.3V3, DHT1.VDD, Part2.VCC, J1.vcc
  GND: U1.GND, DHT1.GND, Part2.GND, J1.gnd
  N3: U1.A0, Part2.AO
  N4: Part1.POS, Part2.POS
  N5: Part1.NEG, Part2.NEG

custom parts:
  NodeMCU V1.0: ESP8266 based NodeMCU
  DHT11 Humitidy and Temperature Sensor: DHT11 Humidity and Temperature Sensor
  FC-28 Soil Hygrometer Module - Probe: The FC-28 is a soil hygrometer module that uses the Texas Instruments LM393 comparator chip to provide an analog measurement of soil humidity.
  FC-28 Soil Hygrometer Module: The FC-28 is a soil hygrometer module that uses the Texas Instruments LM393 comparator chip to provide an analog measurement of soil humidity. The digital output is high when soil moisture is over a certain threshold, as determined by adjusting the potentiometer.
